# Fritzing sketch DisplayBoardTester (saved by Fritzing 0.9.10b)
breadboards: 1

parts:
  Part1 = Arduino Nano (Rev3.0)
  IC1 = IC, DIP package, 16 pins [chip_label="DIL16 Socket"]
  R3 = Resistor [tolerance=±5% power=0.25 resistance=22k package=THT]
  R4 = Resistor [tolerance=±5% power=0.25 resistance=22k package=THT]
  R5 = Resistor [tolerance=±5% power=0.25 resistance=22k package=THT]
  R6 = Resistor [tolerance=±5% power=0.25 resistance=22k package=THT]
  R7 = Resistor [tolerance=±5% power=0.25 resistance=10k package=THT]
  R8 = Resistor [tolerance=±5% power=0.25 resistance=10k package=THT]
  R9 = Resistor [tolerance=±5% power=0.25 resistance=10k package=THT]
  R10 = Resistor [tolerance=±5% power=0.25 resistance=4700 package=THT]

nets:
  GND: Part1.GND, IC1.pin5, IC1.pin16, R3.Pin_0, R4.Pin_0, R5.Pin_0, R6.Pin_0, R7.Pin_1, R10.Pin_1
  N1: Part1.D2, IC1.pin12, R6.Pin_1
  N2: Part1.D3, IC1.pin11, R5.Pin_1
  N3: Part1.D4, IC1.pin10, R4.Pin_1
  N4: Part1.D5, IC1.pin9, R3.Pin_1
  RESET: Part1.D6, IC1.pin4, R10.Pin_0
  C/D: Part1.D7, IC1.pin2
  CS: Part1.D8, IC1.pin15
  CLOCK: Part1.D9, IC1.pin3
  MOSI: Part1.D11/MOSI, IC1.pin14
  5V: Part1.5V, IC1.pin1, IC1.pin8, R9.Pin_1
  SCK: Part1.D13/SCK, IC1.pin13
  3.3V: IC1.pin6, R8.Pin_0, R9.Pin_0
  1.66V: IC1.pin7, R7.Pin_0, R8.Pin_1
